// Logisim project subcircuit.circ as structural Verilog: 6 circuits, main circuit main
module main (
  input  in_1,
  input  in_2,
  output out_3
);

  NAND nand_1 (.in_1(in_1), .in_2(in_2), .out_3(out_3));
endmodule

module NAND (
  input  in_1,
  input  in_2,
  output out_3
);

  wire and_1_out;

  and and_1 (and_1_out, in_1, in_2);
  not not_1 (out_3, and_1_out);
endmodule

module NOR (
  input  in_1,
  input  in_2,
  output out_3
);

  wire or_1_out;

  or or_1 (or_1_out, in_1, in_2);
  not not_1 (out_3, or_1_out);
endmodule

module XOR (
  input  in_1,
  input  in_2,
  output out_3
);

  wire nand_1_out_3, or_1_out;

  NAND nand_1 (.in_1(in_1), .in_2(in_2), .out_3(nand_1_out_3));
  or or_1 (or_1_out, in_1, in_2);
  and and_1 (out_3, or_1_out, nand_1_out_3);
endmodule

module _2TO1MUX (
  input  in_1,
  input  in_2,
  input  in_3,
  output out_4
);

  wire and_1_out, and_2_out, not_1_out;

  not not_1 (not_1_out, in_2);
  and and_1 (and_1_out, not_1_out, in_1);
  and and_2 (and_2_out, in_2, in_3);
  or or_1 (out_4, and_1_out, and_2_out);
endmodule

module _4TO1MUX (
  input  in_1,
  input  in_2,
  input  in_3,
  input  in_4,
  input  in_5,
  input  in_6,
  output out_7
);

  wire n2to1mux_1_out_4, n2to1mux_2_out_4;

  _2TO1MUX u_2to1mux_1 (.in_1(in_1), .in_2(in_5), .in_3(in_2), .out_4(n2to1mux_1_out_4));
  _2TO1MUX u_2to1mux_2 (.in_1(in_3), .in_2(in_5), .in_3(in_4), .out_4(n2to1mux_2_out_4));
  _2TO1MUX u_2to1mux_3 (.in_1(n2to1mux_1_out_4), .in_2(in_6), .in_3(n2to1mux_2_out_4), .out_4(out_7));
endmodule
