// Logisim project advanced_logisim.circ as structural Verilog: 7 circuits, main circuit main
module main (
  input  [3:0] Roll_Amount,
  input  [15:0] In,
  output [15:0] Out
);

  rotr rotr_1 (.Roll_Amount(Roll_Amount), .In(In), .Out(Out));
endmodule

module Ex1 (
  input  [7:0] Input,
  output Out1,
  output [7:0] Out2
);

  not not_1 (Out2[7], Input[7]);
  and and_1 (Out1, Input[0], Input[7]);

  assign Out2[6:0] = Input[6:0];
endmodule

module rotr (
  input  [3:0] Roll_Amount,
  input  [15:0] In,
  output [15:0] Out
);

  wire [15:0] roll2_1_out, roll4_1_out, roll8_1_out;

  roll8 roll8_1 (.In(In), .Select(Roll_Amount[3]), .Out(roll8_1_out));
  roll4 roll4_1 (.In(roll8_1_out), .Select(Roll_Amount[2]), .Out(roll4_1_out));
  roll2 roll2_1 (.In(roll4_1_out), .Select(Roll_Amount[1]), .Out(roll2_1_out));
  roll1 roll1_1 (.In(roll2_1_out), .Select(Roll_Amount[0]), .Out(Out));
endmodule

module roll1 (
  input  Select,
  input  [15:0] In,
  output [15:0] Out
);

  Multiplexer #(.width(16), .enable("false")) multiplexer_1 (
    .in0(In), .in1({In[0], In[15:1]}), .out(Out), .sel(Select));
endmodule

module roll2 (
  input  Select,
  input  [15:0] In,
  output [15:0] Out
);

  Multiplexer #(.width(16), .enable("false")) multiplexer_1 (
    .in0(In), .in1({In[1:0], In[15:2]}), .out(Out), .sel(Select));
endmodule

module roll4 (
  input  Select,
  input  [15:0] In,
  output [15:0] Out
);

  Multiplexer #(.width(16), .enable("false")) multiplexer_1 (
    .in0(In), .in1({In[3:0], In[15:4]}), .out(Out), .sel(Select));
endmodule

module roll8 (
  input  Select,
  input  [15:0] In,
  output [15:0] Out
);

  Multiplexer #(.width(16), .enable("false")) multiplexer_1 (
    .in0(In), .in1({In[7:0], In[15:8]}), .out(Out), .sel(Select));
endmodule
