// Logisim project fib15.circ as structural Verilog: 2 circuits, main circuit main
module fib (
  input  [3:0] Input,
  output [9:0] Output
);

  wire Clock, comparator_1_eq, comparator_2_eq, comparator_2_gt, comparator_3_eq, not_1_out, Stop;
  wire [3:0] index;
  wire [9:0] A_q, adder_1_out, B_in, B_out;

  Comparator #(.width(4)) comparator_1 (.a(index), .b(4'b1111), .eq(comparator_1_eq));  // open: gt, lt
  Register #(.width(10)) A (.D(adder_1_out), .Q(A_q), .clk(Clock));  // open: en, clr
  Comparator #(.width(4), .mode("unsigned")) comparator_2 (
    .a(index), .b(Input), .gt(comparator_2_gt), .eq(comparator_2_eq));  // open: lt
  not not_1 (not_1_out, comparator_1_eq);
  Register #(.width(10)) B (.D(A_q), .Q(B_in), .clk(Clock));  // open: en, clr
  nor nor_1 (Stop, comparator_2_gt, comparator_2_eq);
  Counter #(.width(4), .max('hf)) counter_1 (
    .load(comparator_1_eq), .D(index), .count(not_1_out), .Q(index), .clk(Clock));  // open: carry, clr
  Adder #(.width(10)) adder_1 (.a(A_q), .b(B_out), .out(adder_1_out));  // open: cin, cout
  Clock clock_1 (.out(Clock));
  Register #(.width(10)) C (.D(adder_1_out), .en(Stop), .Q(Output), .clk(Clock));  // open: clr
  Multiplexer #(.width(10), .enable("false")) multiplexer_1 (
    .in0(B_in), .in1(10'h1), .out(B_out), .sel(comparator_3_eq));
  Comparator #(.width(4), .mode("unsigned")) comparator_3 (
    .a(4'b0000), .b(index), .eq(comparator_3_eq));  // open: gt, lt
endmodule

module main (
  input  [3:0] in_1,
  output [9:0] out_2
);

  // Probe on in_1
  fib fib_1 (.Input(in_1), .Output(out_2));
  // Probe on out_2
endmodule
