// Logisim project alu.circ as structural Verilog: 4 circuits, main circuit main
module main (
  input  [31:0] X,
  input  [31:0] Y,
  input  [5:0] Switch__S,
  output Signed_Overflow,
  output [31:0] RESULT,
  output Equal
);

  wire bitselector_1_out, bitselector_2_out, bitselector_3_out, comparator_2_lt, comparator_3_lt;
  wire [4:0] adder_3_out, bit_extender_1_out, bit_extender_2_out, bit_extender_3_out, Transformed_Input;
  wire [31:0] add, addu, \and , bitpal, lfsr, \or , sll, slt, sltu, sra, srl, sub, subu;

  // Probe on X
  // Probe on Y
  Comparator #(.width(32), .mode("unsigned")) comparator_1 (.a(X), .b(Y), .eq(Equal));  // open: gt, lt
  Bit_Extender #(.in_width(32), .out_width(5)) bit_extender_1 (.in(Y), .out(bit_extender_1_out));
  Bit_Extender #(.in_width(32), .out_width(5)) bit_extender_2 (.in(Y), .out(bit_extender_2_out));
  Bit_Extender #(.in_width(32), .out_width(5)) bit_extender_3 (.in(Y), .out(bit_extender_3_out));
  Adder #(.width(32)) adder_1 (.a(X), .b(Y), .out(add));  // open: cin, cout
  Adder #(.width(32)) adder_2 (.a(X), .b(Y), .out(addu));  // open: cin, cout
  Subtractor #(.width(32)) subtractor_1 (.a(X), .b(Y), .out(sub));  // open: bin, bout
  Shifter #(.width(32)) shifter_1 (.in(X), .\dist (bit_extender_1_out), .out(sll));
  Shifter #(.width(32), .shift("lr")) shifter_2 (.in(X), .\dist (bit_extender_2_out), .out(srl));
  Shifter #(.width(32), .shift("ar")) shifter_3 (.in(X), .\dist (bit_extender_3_out), .out(sra));
  Adder #(.width(5)) adder_3 (.a(5'b10111), .b(Switch__S[4:0]), .out(adder_3_out));  // open: cin, cout
  Comparator #(.width(32)) comparator_2 (.a(X), .b(Y), .lt(comparator_2_lt));  // open: gt, eq
  Comparator #(.width(32), .mode("unsigned")) comparator_3 (.a(X), .b(Y), .lt(comparator_3_lt));  // open: gt, eq
  bitpal bitpal_1 (.Input(X), .Output(bitpal));
  lfsr lfsr_1 (.Input(X), .Output(lfsr));
  Subtractor #(.width(32)) subtractor_2 (.a(X), .b(Y), .out(subu));  // open: bin, bout
  assign \and  = X & Y;  // AND_Gate and_1, 32 bits wide
  assign \or  = X | Y;  // OR_Gate or_1, 32 bits wide
  Multiplexer #(.width(5), .enable("false")) multiplexer_1 (
    .in0(adder_3_out), .in1(Switch__S[4:0]), .out(Transformed_Input), .sel(Switch__S[5]));
  assign slt = {{31{1'b0}}, comparator_2_lt};  // Bit_Extender bit_extender_4
  assign sltu = {{31{1'b0}}, comparator_3_lt};  // Bit_Extender bit_extender_5
  // Probe on RESULT
  BitSelector #(.width(32)) bitselector_1 (.in(RESULT), .out(bitselector_1_out), .sel({5{1'b1}}));
  BitSelector #(.width(32)) bitselector_2 (.in(X), .out(bitselector_2_out), .sel({5{1'b1}}));
  BitSelector #(.width(32)) bitselector_3 (.in(Y), .out(bitselector_3_out), .sel({5{1'b1}}));
  overflow_checker Overflow_Checker (
    .Result_Most_Significant_Bit(bitselector_1_out), .X_Most_Significant_Bit(bitselector_2_out),
    .Y_Most_Significant_Bit(bitselector_3_out), .Input(Switch__S), .Signed_Overflow(Signed_Overflow));
  Multiplexer #(.select(5), .width(32), .enable("false")) multiplexer_2 (
    .in0(add), .in1(addu), .in2(sub), .in3(subu), .in4(\and ), .in5(\or ), .in10(slt), .in11(sltu),
    .in23(sll), .in25(srl), .in26(sra), .in30(bitpal), .in31(lfsr), .out(RESULT), .sel(Transformed_Input));  // open: in6, in7, in8, in9, in12, in13, in14, in15, in16, in17, in18, in19, in20, in21, in22, in24, in27, in28, in29

  // Other names for the same wires on the sheet: Input[5:0] = Switch__S; S_Overflow = Signed_Overflow

  // Notes on the sheet:
  //   INPUT to your circuit
  //   INPUTS to your circuit
  //   EQUALITY CHECK
  //   ALU FUNCTIONS
  //   MAX 5 BIT MUX, HAVE TO TRANSFORM INPUT
  //   DON'T CHANGE THE INPUTS AND OUTPUTS! IF YOU DO SO, YOU NEED TO MAKE SURE THE PINS ARE IN THE RIGHT PLACES!
  //   OUTPUTS of your circuit
  //   SELECT THE REQUESTED RESULT
endmodule

module overflow_checker (
  input  Result_Most_Significant_Bit,
  input  X_Most_Significant_Bit,
  input  Y_Most_Significant_Bit,
  input  [5:0] Input,
  output Signed_Overflow
);

  wire and_1_out, and_2_out, and_3_out, and_4_out, and_5_out, comparator_1_eq, comparator_2_eq,
       comparator_3_eq, or_1_out, xor_1_out;

  Comparator #(.width(6), .mode("unsigned")) comparator_1 (
    .a(Input), .b(6'b100010), .eq(comparator_1_eq));  // open: gt, lt
  and and_1 (and_1_out, ~Result_Most_Significant_Bit, X_Most_Significant_Bit, Y_Most_Significant_Bit);  // AND_Gate
  and and_2 (and_2_out, Result_Most_Significant_Bit, ~X_Most_Significant_Bit, ~Y_Most_Significant_Bit);  // AND_Gate
  Comparator #(.width(6), .mode("unsigned")) comparator_2 (
    .a(Input), .b(6'b100000), .eq(comparator_2_eq));  // open: gt, lt
  Comparator #(.width(1), .mode("unsigned")) comparator_3 (
    .a(Result_Most_Significant_Bit), .b(Y_Most_Significant_Bit), .eq(comparator_3_eq));  // open: gt, lt
  xor xor_1 (xor_1_out, X_Most_Significant_Bit, Y_Most_Significant_Bit);
  or or_1 (or_1_out, and_1_out, and_2_out);
  and and_3 (and_3_out, comparator_3_eq, xor_1_out);
  and and_4 (and_4_out, or_1_out, comparator_2_eq);
  and and_5 (and_5_out, and_3_out, comparator_1_eq);
  or or_2 (Signed_Overflow, and_4_out, and_5_out);

  // Other names for the same wires on the sheet: Result = Result_Most_Significant_Bit; X = X_Most_Significant_Bit;
  //   Y = Y_Most_Significant_Bit

  // Notes on the sheet:
  //   ADDITION OVERFLOW
  //   SUBTRACTION OVERFLOW
endmodule

module bitpal (
  input  [31:0] Input,
  output [31:0] Output
);

  wire comparator_1_eq;

  Comparator #(.width(16), .mode("unsigned")) comparator_1 (
    .a({Input[0], Input[1], Input[2], Input[3], Input[4], Input[5], Input[6], Input[7], Input[8], Input[9], Input[10], Input[11], Input[12], Input[13], Input[14], Input[15]}),
    .b(Input[31:16]), .eq(comparator_1_eq));  // open: gt, lt
  assign Output = {{31{1'b0}}, comparator_1_eq};  // Bit_Extender bit_extender_1
endmodule

module lfsr (
  input  [31:0] Input,
  output [31:0] Output
);

  wire xor_1_out, xor_2_out;
  wire [14:0] bit_extender_2_out;
  wire [15:0] bit_extender_1_out, shifter_1_out;
  wire [15:15] xor_3_out;

  // Probe on Input
  Bit_Extender #(.in_width(32)) bit_extender_1 (.in(Input), .out(bit_extender_1_out));
  Shifter #(.width(16), .shift("lr")) shifter_1 (.in(bit_extender_1_out), .\dist (4'b0001), .out(shifter_1_out));
  xor xor_1 (xor_1_out, bit_extender_1_out[0], bit_extender_1_out[2]);
  xor xor_2 (xor_2_out, xor_1_out, bit_extender_1_out[3]);
  Bit_Extender #(.in_width(16), .out_width(15)) bit_extender_2 (.in(shifter_1_out), .out(bit_extender_2_out));
  xor xor_3 (xor_3_out[15], xor_2_out, bit_extender_1_out[5]);
  assign Output = {{16{1'b0}}, {xor_3_out[15], bit_extender_2_out}};  // Bit_Extender bit_extender_3
  // Probe on Output
endmodule
