// Logisim project cpu.circ as structural Verilog: 7 circuits, main circuit main
module main (
  input  [31:0] RS_READ_VALUE,
  input  [31:0] RT_READ_VALUE,
  input  [31:0] INSTRUCTION,
  input  CLOCK,
  input  RESET,
  output [31:0] t0,
  output [31:0] t1,
  output [31:0] t2,
  output [31:0] t3,
  output [4:0] RS,
  output [4:0] RT,
  output [4:0] Write_Register,
  output [31:0] RD_WRITE_VALUE,
  output RD_WRITE_ENABLE,
  output [23:0] FETCH_ADDRESS
);

  wire AccessByte, comparator_1_gt, Equal, execute_stage_1_signed_overflow, ExtOp, MemWr, Nop, not_1_out,
       nPC_sel, RegWr;
  wire [1:0] ALUSrc, Branch, Jump, RegDst;
  wire [2:0] MemToReg;
  wire [4:0] Shamt;
  wire [5:0] ALUctr;
  wire [15:0] Imm16;
  wire [23:0] PcPlusOne, PipelinedPC;
  wire [25:0] JumpTarget;
  wire [31:0] AluResult, Bus_A, Bus_B, DataOut, multiplexer_1_out, PipelinedInstruction, WriteData;

  Multiplexer #(.width(32), .disabled(0), .enable("false")) multiplexer_1 (
    .in0(INSTRUCTION), .in1({32{1'b0}}), .out(multiplexer_1_out), .sel(Nop));
  Register #(.width(24)) PC_Plus_One (.D(PcPlusOne), .Q(PipelinedPC), .clk(CLOCK));  // open: en, clr
  Register #(.width(32)) u_Instruction (.D(multiplexer_1_out), .Q(PipelinedInstruction), .clk(CLOCK));  // open: en, clr
  Comparator #(.width(2), .mode("unsigned")) comparator_1 (.a(Jump), .b(2'b00), .gt(comparator_1_gt));  // open: eq, lt
  or or_1 (Nop, nPC_sel, comparator_1_gt);
  instruction_fetch instruction_fetch_1 (
    .Jump_Target(JumpTarget), .RS(Bus_A), .Imm_16(Imm16), .nPC_sel(nPC_sel), .Jump(Jump), .CLOCK(CLOCK),
    .FetchAddress(FETCH_ADDRESS), .PC_Plus_1(PcPlusOne));
  control control_1 (
    .Instruction(PipelinedInstruction), .RegDst(RegDst), .RegWrite(RegWr), .MemWrite(MemWr), .ExtOp(ExtOp),
    .AccessByte(AccessByte), .ALUctr(ALUctr), .ALUSrc(ALUSrc), .Jump(Jump), .Branch(Branch),
    .MemToReg(MemToReg));
  instruction_decode instruction_decode_1 (
    .RS_READ_VALUE(RS_READ_VALUE), .RT_READ_VALUE(RT_READ_VALUE), .WRITE_DATA(WriteData),
    .Instruction(PipelinedInstruction), .REG_DST(RegDst), .CLOCK(CLOCK), .WRITE_ENABLED(RegWr),
    .t0_Value(t0), .t1_Value(t1), .t2_Value(t2), .t3_Value(t3), .JumpTarget(JumpTarget), .Shamt(Shamt),
    .RS(RS), .RT(RT), .Write_Register(Write_Register), .Write_Value(RD_WRITE_VALUE),
    .WRITE_ENABLE(RD_WRITE_ENABLE), .Bus_A(Bus_A), .Bus_B(Bus_B), .Imm_Output(Imm16));
  not not_1 (not_1_out, Equal);
  mem_main main_1 (
    .Data_Mem_Addr(AluResult), .Data_Mem_In(Bus_B), .ACCESS_BYTE(AccessByte), .MEM_WRITE(MemWr),
    .CLOCK(CLOCK), .Data_Mem_Out(DataOut));
  write_back write_back_1 (
    .ALU_RESULT(AluResult), .DATA_OUT(DataOut), .IMM_16(Imm16), .PC_VALUE(PipelinedPC),
    .MEM_TO_REG(MemToReg), .WRITE_BACK(WriteData));
  LED Signed_Overflow (.in(execute_stage_1_signed_overflow));
  execute_stage execute_stage_1 (
    .BUS_A(Bus_A), .BUS_B(Bus_B), .IMM_16(Imm16), .Shamt(Shamt), .ExtOp(ExtOp), .ALUSrc(ALUSrc),
    .ALUctr(ALUctr), .Signed_Overflow(execute_stage_1_signed_overflow), .RESULT(AluResult), .Equal(Equal));
  Multiplexer #(.select(2), .disabled(0), .enable("false")) multiplexer_2 (
    .in0(1'b0), .in1(Equal), .in2(not_1_out), .out(nPC_sel), .sel(Branch));  // open: in3

  // Other names for the same wires on the sheet: FetchAddress[23:0] = FETCH_ADDRESS; RdWriteEnable = RD_WRITE_ENABLE;
  //   RdWriteValue[31:0] = RD_WRITE_VALUE; RsReadValue[31:0] = RS_READ_VALUE; RtReadValue[31:0] = RT_READ_VALUE;
  //   WriteRegister[4:0] = Write_Register

  // Notes on the sheet:
  //   Handle Pipelining
  //   These are outputs/inputs from run.circ
  //   Instruction Fetch
  //   Control Section
  //   These are outputs to run.circ
  //   Instruction Decode
  //   Memory Access
  //   Write Back
  //   ALU
endmodule

module instruction_fetch (
  input  [25:0] Jump_Target,
  input  [31:0] RS,
  input  [15:0] Imm_16,
  input  nPC_sel,
  input  [1:0] Jump,
  input  CLOCK,
  output [23:0] FetchAddress,
  output [23:0] PC_Plus_1
);

  wire [23:0] adder_2_out, AddressInReg, bit_extender_1_out, JumpAddress, multiplexer_1_out,
       multiplexer_2_out;
  wire [25:24] subtractor_1_out;
  wire [31:24] subtractor_2_out;

  assign bit_extender_1_out = {{8{Imm_16[15]}}, Imm_16};  // Bit_Extender bit_extender_1
  Adder #(.width(24)) adder_1 (.a(FetchAddress), .b(24'h1), .out(PC_Plus_1));  // open: cin, cout
  Adder #(.width(24)) adder_2 (.a(FetchAddress), .b(bit_extender_1_out), .out(adder_2_out));  // open: cin, cout
  Multiplexer #(.width(24), .disabled(0), .enable("false")) multiplexer_1 (
    .in0(PC_Plus_1), .in1(adder_2_out), .out(multiplexer_1_out), .sel(nPC_sel));
  Subtractor #(.width(26)) subtractor_1 (
    .a(Jump_Target), .b(26'h100000), .out({subtractor_1_out, JumpAddress}));  // open: bin, bout
  Subtractor #(.width(32)) subtractor_2 (
    .a(RS), .b(32'h100000), .out({subtractor_2_out, AddressInReg}));  // open: bin, bout
  Multiplexer #(.select(2), .width(24), .disabled(0), .enable("false")) multiplexer_2 (
    .in0(multiplexer_1_out), .in1(JumpAddress), .in2(AddressInReg), .out(multiplexer_2_out), .sel(Jump));  // open: in3
  Register #(.width(24)) PC (.D(multiplexer_2_out), .Q(FetchAddress), .clk(CLOCK));  // open: en, clr

  // Other names for the same wires on the sheet: Imm16[15:0] = Imm_16; JumpTarget[25:0] = Jump_Target;
  //   NextPC[23:0] = PC_Plus_1; nPCSel = nPC_sel

  // Notes on the sheet:
  //   INPUTS
  //   INSTRUCTION FETCH LOGIC
  //   OUTPUT
  //   Address Transformer
  //   Address Transformer RS
endmodule

module instruction_decode (
  input  [31:0] RS_READ_VALUE,
  input  [31:0] RT_READ_VALUE,
  input  [31:0] WRITE_DATA,
  input  [31:0] Instruction,
  input  [1:0] REG_DST,
  input  CLOCK,
  input  WRITE_ENABLED,
  output [4:0] RS,
  output [4:0] RT,
  output [4:0] Write_Register,
  output [31:0] t0_Value,
  output [31:0] t1_Value,
  output [31:0] t2_Value,
  output [31:0] t3_Value,
  output [31:0] Write_Value,
  output WRITE_ENABLE,
  output [25:0] JumpTarget,
  output [4:0] Shamt,
  output [31:0] Bus_A,
  output [31:0] Bus_B,
  output [15:0] Imm_Output
);

  wire EnableWriteOwnRegFile, RsOwnRegFile, RtOwnRegFile, WriteRegOwnRegFile;
  wire [1:0] ModifiedRs, ModifiedRt, ModifiedWriteReg;
  wire [4:0] subtractor_1_out, subtractor_2_out, subtractor_3_out;
  wire [31:0] main_1_read_data_1, main_1_read_data_2;

  and and_1 (EnableWriteOwnRegFile, WRITE_ENABLED, WriteRegOwnRegFile);
  regfile_main main_1 (
    .Read_register_1(ModifiedRs), .Read_register_2(ModifiedRt), .write_register(ModifiedWriteReg),
    .write_data(WRITE_DATA), .t0_Value(t0_Value), .t1_Value(t1_Value), .t2_Value(t2_Value),
    .t3_Value(t3_Value), .RegWrite(EnableWriteOwnRegFile), .clock(CLOCK), .Read_Data_1(main_1_read_data_1),
    .Read_Data_2(main_1_read_data_2));
  Bit_Extender #(.in_width(5), .out_width(2)) bit_extender_1 (.in(subtractor_1_out), .out(ModifiedRs));
  Subtractor #(.width(5)) subtractor_1 (
    .a(Instruction[25:21]), .b(5'b01000), .out(subtractor_1_out));  // open: bin, bout
  Bit_Extender #(.in_width(5), .out_width(2)) bit_extender_2 (.in(subtractor_2_out), .out(ModifiedRt));
  Subtractor #(.width(5)) subtractor_2 (
    .a(Instruction[20:16]), .b(5'b01000), .out(subtractor_2_out));  // open: bin, bout
  Bit_Extender #(.in_width(5), .out_width(2)) bit_extender_3 (.in(subtractor_3_out), .out(ModifiedWriteReg));
  Subtractor #(.width(5)) subtractor_3 (.a(Write_Register), .b(5'b01000), .out(subtractor_3_out));  // open: bin, bout
  Multiplexer #(.width(32), .disabled(0), .enable("false")) multiplexer_1 (
    .in0(RS_READ_VALUE), .in1(main_1_read_data_1), .out(Bus_A), .sel(RsOwnRegFile));
  Multiplexer #(.width(32), .disabled(0), .enable("false")) multiplexer_2 (
    .in0(RT_READ_VALUE), .in1(main_1_read_data_2), .out(Bus_B), .sel(RtOwnRegFile));
  Multiplexer #(.select(2), .width(5), .disabled(0), .enable("false")) multiplexer_3 (
    .in0(Instruction[20:16]), .in1(Instruction[15:11]), .in2({5{1'b1}}), .out(Write_Register), .sel(REG_DST));  // open: in3
  temp_reg_checker temp_reg_checker_1 (.Reg_Number(Write_Register), .Use_My_Reg_File(WriteRegOwnRegFile));
  temp_reg_checker temp_reg_checker_2 (.Reg_Number(Instruction[25:21]), .Use_My_Reg_File(RsOwnRegFile));
  temp_reg_checker temp_reg_checker_3 (.Reg_Number(Instruction[20:16]), .Use_My_Reg_File(RtOwnRegFile));

  assign Imm_Output = Instruction[15:0];
  assign JumpTarget = Instruction[25:0];
  assign RS = Instruction[25:21];
  assign RT = Instruction[20:16];
  assign Shamt = Instruction[10:6];
  assign WRITE_ENABLE = WRITE_ENABLED;
  assign Write_Value = WRITE_DATA;

  // Other names for the same wires on the sheet: BusA[31:0] = Bus_A; BusB[31:0] = Bus_B;
  //   Imm16[15:0] = Instruction[15:0]; Rd[4:0] = Instruction[15:11]; RegDst[1:0] = REG_DST;
  //   RsReadValue[31:0] = RS_READ_VALUE; RtReadValue[31:0] = RT_READ_VALUE; t0_Out[31:0] = t0_Value;
  //   t1_Out[31:0] = t1_Value; t2_Out[31:0] = t2_Value; t3_Out[31:0] = t3_Value; WriteData[31:0] = WRITE_DATA;
  //   WriteEnable = WRITE_ENABLED; WriteReg[4:0] = Write_Register

  // Notes on the sheet:
  //   These are OUTPUTS to the circuit
  //   Enable Write for My Reg File?
  //   Main Logic for Instruction Decoding with My Reg File
  //   Modify Registers to Use My Reg File
  //   Select Reg to Write
  //   Output Immediate Value
  //   Outputs to Harness Reg File
  //   Use Harness or Own Reg File?
  //   Extracts Fields from Instruction
endmodule

module temp_reg_checker (
  input  [4:0] Reg_Number,
  output Use_My_Reg_File
);

  wire comparator_1_gt, comparator_2_gt;

  Comparator #(.width(5), .mode("unsigned")) comparator_1 (
    .a(5'b01100), .b(Reg_Number), .gt(comparator_1_gt));  // open: eq, lt
  Comparator #(.width(5), .mode("unsigned")) comparator_2 (
    .a(Reg_Number), .b(5'b00111), .gt(comparator_2_gt));  // open: eq, lt
  and and_1 (Use_My_Reg_File, comparator_1_gt, comparator_2_gt);
endmodule

module execute_stage (
  input  [31:0] BUS_A,
  input  [31:0] BUS_B,
  input  [15:0] IMM_16,
  input  [4:0] Shamt,
  input  ExtOp,
  input  [1:0] ALUSrc,
  input  [5:0] ALUctr,
  output Signed_Overflow,
  output [31:0] RESULT,
  output Equal
);

  wire [31:0] bit_extender_1_out, bit_extender_2_out, Imm32, Shamt32, X, Y;

  alu_main main_1 (.Switch__S(ALUctr), .X(X), .Equal(Equal), .RESULT(RESULT), .Signed_Overflow(Signed_Overflow), .Y(Y));
  Multiplexer #(.select(2), .width(32), .disabled(0), .enable("false")) multiplexer_1 (
    .in0(BUS_B), .in1(Imm32), .in2(Shamt32), .out(Y), .sel(ALUSrc));  // open: in3
  Multiplexer #(.select(2), .width(32), .disabled(0), .enable("false")) multiplexer_2 (
    .in0(BUS_A), .in1(BUS_A), .in2(BUS_B), .out(X), .sel(ALUSrc));  // open: in3
  assign bit_extender_1_out = {{16{1'b0}}, IMM_16};  // Bit_Extender bit_extender_1
  assign bit_extender_2_out = {{16{IMM_16[15]}}, IMM_16};  // Bit_Extender bit_extender_2
  assign Shamt32 = {{27{1'b0}}, Shamt};  // Bit_Extender bit_extender_3
  Multiplexer #(.width(32), .disabled(0), .enable("false")) multiplexer_3 (
    .in0(bit_extender_1_out), .in1(bit_extender_2_out), .out(Imm32), .sel(ExtOp));

  // Other names for the same wires on the sheet: BusA[31:0] = BUS_A; BusB[31:0] = BUS_B; Imm16[15:0] = IMM_16;
  //   S_Overflow = Signed_Overflow

  // Notes on the sheet:
  //   INPUTS of your circuit
  //   Calculate Result
  //   Get Source for Y
  //   Get Source for X
  //   Get Immediate
  //   Shamt Extender
  //   OUTPUTS of your circuit
endmodule

module control (
  input  [31:0] Instruction,
  output [1:0] RegDst,
  output RegWrite,
  output MemWrite,
  output ExtOp,
  output AccessByte,
  output [5:0] ALUctr,
  output [1:0] ALUSrc,
  output [1:0] Jump,
  output [1:0] Branch,
  output [2:0] MemToReg
);

  wire addiu_out, ALUOp0, ALUOp1, andi_2_out, andi_out, beq_2_out, bne_2_out, comparator_1_eq,
       comparator_2_eq, comparator_4_gt, comparator_5_eq, j_out, lb_out, lbu_out, lui_out, lw_out, or_2_out,
       ori_2_out, ori_out, sll_out, sra_out, srl_out;
  wire [5:0] multiplexer_1_out;

  Comparator #(.width(6), .mode("unsigned")) comparator_1 (
    .a(Instruction[31:26]), .b(6'b100000), .eq(comparator_1_eq));  // open: gt, lt
  Comparator #(.width(6), .mode("unsigned")) comparator_2 (
    .a(Instruction[31:26]), .b(6'b100100), .eq(comparator_2_eq));  // open: gt, lt
  Comparator #(.width(6), .mode("unsigned")) comparator_3 (
    .a(Instruction[5:0]), .b(6'b001000), .eq(Jump[1]));  // open: gt, lt
  and R_Type (RegDst[0], ~Instruction[31], ~Instruction[30], ~Instruction[29], ~Instruction[28], ~Instruction[27], ~Instruction[26]);  // AND_Gate
  or or_1 (AccessByte, comparator_1_eq, comparator_2_eq);
  and lw (lw_out, Instruction[31], ~Instruction[30], ~Instruction[29], ~Instruction[28], Instruction[27], Instruction[26]);  // AND_Gate
  and sw (MemWrite, Instruction[31], ~Instruction[30], Instruction[29], ~Instruction[28], Instruction[27], Instruction[26]);  // AND_Gate
  Multiplexer #(.select(2), .width(6), .disabled(0), .enable("false")) multiplexer_1 (
    .in0(6'b100000), .in1(6'b100010), .in2(6'b100100), .in3(6'b100101), .out(multiplexer_1_out),
    .sel({ALUOp1, ALUOp0}));
  Comparator #(.width(6), .mode("unsigned")) comparator_4 (
    .a(Instruction[31:26]), .b({6{1'b0}}), .gt(comparator_4_gt));  // open: eq, lt
  and beq (Branch[0], ~Instruction[31], ~Instruction[30], ~Instruction[29], Instruction[28], ~Instruction[27], ~Instruction[26]);  // AND_Gate
  and j (j_out, ~Instruction[31], ~Instruction[30], ~Instruction[29], ~Instruction[28], Instruction[27], ~Instruction[26]);  // AND_Gate
  Multiplexer #(.width(6), .disabled(0), .enable("false")) multiplexer_2 (
    .in0(Instruction[5:0]), .in1(multiplexer_1_out), .out(ALUctr), .sel(comparator_4_gt));
  and sll (sll_out, ~Instruction[5], ~Instruction[4], ~Instruction[3], ~Instruction[2], ~Instruction[1], ~Instruction[0]);  // AND_Gate
  and jal (MemToReg[2], ~Instruction[31], ~Instruction[30], ~Instruction[29], ~Instruction[28], Instruction[27], Instruction[26]);  // AND_Gate
  and srl (srl_out, ~Instruction[5], ~Instruction[4], ~Instruction[3], ~Instruction[2], Instruction[1], ~Instruction[0]);  // AND_Gate
  and bne (Branch[1], ~Instruction[31], ~Instruction[30], ~Instruction[29], Instruction[28], ~Instruction[27], Instruction[26]);  // AND_Gate
  and sra (sra_out, ~Instruction[5], ~Instruction[4], ~Instruction[3], ~Instruction[2], Instruction[1], Instruction[0]);  // AND_Gate
  and lbu (lbu_out, Instruction[31], ~Instruction[30], ~Instruction[29], Instruction[28], ~Instruction[27], ~Instruction[26]);  // AND_Gate
  or or_2 (or_2_out, sll_out, srl_out, sra_out);
  Comparator #(.width(6), .mode("unsigned")) comparator_5 (
    .a(Instruction[31:26]), .b({6{1'b0}}), .eq(comparator_5_eq));  // open: gt, lt
  and lui (lui_out, ~Instruction[31], ~Instruction[30], Instruction[29], Instruction[28], Instruction[27], Instruction[26]);  // AND_Gate
  and and_1 (ALUSrc[1], or_2_out, comparator_5_eq);
  and lb (lb_out, Instruction[31], ~Instruction[30], ~Instruction[29], ~Instruction[28], ~Instruction[27], ~Instruction[26]);  // AND_Gate
  and ori (ori_out, ~Instruction[31], ~Instruction[30], Instruction[29], Instruction[28], ~Instruction[27], Instruction[26]);  // AND_Gate
  and andi (andi_out, ~Instruction[31], ~Instruction[30], Instruction[29], Instruction[28], ~Instruction[27], ~Instruction[26]);  // AND_Gate
  and andi_2 (andi_2_out, ~Instruction[31], ~Instruction[30], Instruction[29], Instruction[28], ~Instruction[27], ~Instruction[26]);  // AND_Gate
  and ori_2 (ori_2_out, ~Instruction[31], ~Instruction[30], Instruction[29], Instruction[28], ~Instruction[27], Instruction[26]);  // AND_Gate
  and addiu (addiu_out, ~Instruction[31], ~Instruction[30], Instruction[29], ~Instruction[28], ~Instruction[27], Instruction[26]);  // AND_Gate
  and beq_2 (beq_2_out, ~Instruction[31], ~Instruction[30], ~Instruction[29], Instruction[28], ~Instruction[27], ~Instruction[26]);  // AND_Gate
  and bne_2 (bne_2_out, ~Instruction[31], ~Instruction[30], ~Instruction[29], Instruction[28], ~Instruction[27], Instruction[26]);  // AND_Gate
  or or_3 (ALUSrc[0], andi_2_out, lw_out, lbu_out, ori_out, lb_out, MemWrite, addiu_out);
  or or_4 (MemToReg[0], lw_out, lbu_out, lui_out);
  or or_5 (MemToReg[1], lb_out, lui_out);
  or or_6 (RegWrite, lb_out, ori_out, RegDst[0], lbu_out, MemToReg[2], lui_out, lw_out, andi_2_out, addiu_out);
  or or_7 (ExtOp, lw_out, lbu_out, addiu_out, lb_out, MemWrite);
  or or_8 (Jump[0], j_out, MemToReg[2]);
  or or_9 (ALUOp0, bne_2_out, ori_2_out, beq_2_out);
  or or_10 (ALUOp1, ori_2_out, andi_out);

  assign RegDst[1] = MemToReg[2];

  // Other names for the same wires on the sheet: Function[5:0] = Instruction[5:0]; Opcode[5:0] = Instruction[31:26];
  //   RegDst1 = MemToReg[2]

  // Notes on the sheet:
  //   Byte Access
  //   Select Opcode and Function Field
  //   Jump Register
  //   ALUctr Output
  //   Set ALU Source in Case of Shift Operations
  //   Control Logic
  //   ALU OP for I Type Instruction
  //   Outputs
  //   00 rt; 01 rd; 10 $ra
  //   01 Imm; 10 Shamt
  //   00 Add
  //   01 Sub
  //   10 And
  //   11 Or
  //   01 j&jal; 10 jr
  //   01 beq; 10 bne
  //   001 lw&lbu
  //   010 lb
  //   011 lui
  //   100 jal
endmodule

module write_back (
  input  [31:0] ALU_RESULT,
  input  [31:0] DATA_OUT,
  input  [15:0] IMM_16,
  input  [23:0] PC_VALUE,
  input  [2:0] MEM_TO_REG,
  output [31:0] WRITE_BACK
);

  wire [23:0] adder_1_out;
  wire [31:0] JAL_Output, LB_Output;

  Adder #(.width(24)) adder_1 (.a(PC_VALUE), .b(24'h100000), .out(adder_1_out));  // open: cin, cout
  Multiplexer #(.select(3), .width(32), .disabled(0), .enable("false")) multiplexer_1 (
    .in0(ALU_RESULT), .in1(DATA_OUT), .in2(LB_Output), .in3({IMM_16, {16{1'b0}}}), .in4(JAL_Output),
    .out(WRITE_BACK), .sel(MEM_TO_REG));  // open: in5, in6, in7
  assign LB_Output = {{24{DATA_OUT[7]}}, DATA_OUT[7:0]};  // Bit_Extender bit_extender_1
  assign JAL_Output = {{8{1'b0}}, adder_1_out};  // Bit_Extender bit_extender_2

  // Other names for the same wires on the sheet: AluResult[31:0] = ALU_RESULT; DataOut[31:0] = DATA_OUT;
  //   Imm16[15:0] = IMM_16; LUI_Output[31:16] = IMM_16; MemToReg[2:0] = MEM_TO_REG; PC[23:0] = PC_VALUE;
  //   WriteBackValue[31:0] = WRITE_BACK

  // Notes on the sheet:
  //   INPUTS
  //   Select Output
  //   Calc Output
  //   Output
endmodule
