// Logisim project mem.circ as structural Verilog: 1 circuit, main circuit main
module main (
  input  [31:0] Data_Mem_Addr,
  input  [31:0] Data_Mem_In,
  input  ACCESS_BYTE,
  input  MEM_WRITE,
  input  CLOCK,
  output [31:0] Data_Mem_Out
);

  wire not_1_out;
  wire [1:0] ByteSelector;
  wire [7:0] multiplexer_1_out;
  wire [23:0] Address24;
  wire [31:0] bit_extender_1_out, DataOut;
  wire [31:26] subtractor_1_out;

  Multiplexer #(.select(2), .width(8), .disabled(0), .enable("false")) multiplexer_1 (
    .in0(DataOut[7:0]), .in1(DataOut[15:8]), .in2(DataOut[23:16]), .in3(DataOut[31:24]),
    .out(multiplexer_1_out), .sel(ByteSelector));
  Subtractor #(.width(32)) subtractor_1 (
    .a(Data_Mem_Addr), .b(32'h10010000), .out({subtractor_1_out, Address24, ByteSelector}));  // open: bin, bout
  assign bit_extender_1_out = {{24{1'b0}}, multiplexer_1_out};  // Bit_Extender bit_extender_1
  Multiplexer #(.width(32), .disabled(0), .enable("false")) multiplexer_2 (
    .in0(DataOut), .in1(bit_extender_1_out), .out(Data_Mem_Out), .sel(ACCESS_BYTE));
  assign DataOut = MEM_WRITE ? Data_Mem_In : 32'bz;  // Controlled_Buffer controlled_buffer_1
  not not_1 (not_1_out, MEM_WRITE);
  RAM #(.addrWidth(24), .dataWidth(32)) ram_1 (
    .addr(Address24), .data(DataOut), .sel(1'b1), .clk(CLOCK), .ld(not_1_out), .clr(1'b0));

  // Other names for the same wires on the sheet: AccessByte = ACCESS_BYTE; Address32[31:0] = Data_Mem_Addr;
  //   DataIn[31:0] = Data_Mem_In; FinalDataOut[31:0] = Data_Mem_Out; MemWrite = MEM_WRITE

  // Notes on the sheet:
  //   These are INPUTS to the circuit
  //   These are INPUTS to the circuit
  //   DO NOT CHANGE THE LOCATIONS OF THE INPUTS/OUTPUTS! IF YOU DO SO, YOU NEED TO MAKE SURE THE PINS ARE AT THE RIGHT PLACE!
  //   Byte Selection
  //   Yet again, the clock is not an actual clock, but an input, one that will be driven from a higher circuit
  //   Address Transformer
  //   This is an OUTPUT to the circuit
  //   RAM
endmodule
