// Logisim project regfile.circ as structural Verilog: 1 circuit, main circuit main
module main (
  input  [1:0] Read_register_1,
  input  [1:0] Read_register_2,
  input  [1:0] write_register,
  input  [31:0] write_data,
  input  RegWrite,
  input  clock,
  output [31:0] t0_Value,
  output [31:0] t1_Value,
  output [31:0] t2_Value,
  output [31:0] t3_Value,
  output [31:0] Read_Data_1,
  output [31:0] Read_Data_2
);

  wire Write__t0, Write__t1, Write__t2, Write__t3;

  Register #(.width(32)) t0 (.D(write_data), .en(Write__t0), .Q(t0_Value), .clk(clock));  // open: clr
  Register #(.width(32)) t1 (.D(write_data), .en(Write__t1), .Q(t1_Value), .clk(clock));  // open: clr
  Register #(.width(32)) t2 (.D(write_data), .en(Write__t2), .Q(t2_Value), .clk(clock));  // open: clr
  Register #(.width(32)) t3 (.D(write_data), .en(Write__t3), .Q(t3_Value), .clk(clock));  // open: clr
  Multiplexer #(.select(2), .width(32), .enable("false")) multiplexer_1 (
    .in0(t0_Value), .in1(t1_Value), .in2(t2_Value), .in3(t3_Value), .out(Read_Data_1), .sel(Read_register_1));
  Multiplexer #(.select(2), .width(32), .enable("false")) multiplexer_2 (
    .in0(t0_Value), .in1(t1_Value), .in2(t2_Value), .in3(t3_Value), .out(Read_Data_2), .sel(Read_register_2));
  Decoder #(.select(2), .disabled(0)) decoder_1 (
    .out0(Write__t0), .out1(Write__t1), .out2(Write__t2), .out3(Write__t3), .sel(write_register),
    .en(RegWrite));

  // Other names for the same wires on the sheet: Data_In[31:0] = write_data; Read1[1:0] = Read_register_1;
  //   Read2[1:0] = Read_register_2; t0_Out[31:0] = t0_Value; t1_Out[31:0] = t1_Value; t2_Out[31:0] = t2_Value;
  //   t3_Out[31:0] = t3_Value; Write[1:0] = write_register

  // Notes on the sheet:
  //   These are INPUTS to the circuit
  //   These are INPUTS to the circuit
  //   THE 4 REGISTERS
  //   DO NOT CHANGE THE LOCATIONS OF THE INPUTS/OUTPUTS! IF YOU DO SO, YOU NEED TO MAKE SURE THE PINS ARE AT THE RIGHT PLACE!
  //   These are OUTPUTS to the circuit
  //   Yet again, the clock is not an actual clock, but an input, one that will be driven from a higher circuit
  //   SELECT REGISTER TO WRITE
  //   These are OUTPUTS to the circuit
endmodule
